// Logisim project tower.circ as structural Verilog: 5 circuits, main circuit main
module main (
  input  in_1,
  input  in_2,
  input  in_3,
  input  in_4,
  input  in_5,
  input  in_6,
  input  in_7,
  input  in_8,
  input  in_9,
  input  in_10,
  input  in_11,
  input  in_12,
  input  in_13,
  input  in_14,
  input  in_15,
  input  in_16,
  input  in_17,
  input  in_18,
  input  in_19,
  input  in_20,
  input  in_21,
  input  in_22,
  input  in_23,
  input  in_24,
  input  in_25,
  input  in_26,
  input  in_27,
  input  in_28,
  input  in_29,
  input  in_30,
  input  in_31,
  input  in_32
);

  wire CLK, clock_1_out, F_CARRY, F_SIGN, F_ZERO, RESET;
  wire [1:1] FLAGS;
  wire [3:0] registers_1_f_data_out;
  wire [7:0] DATA_BUS, registers_1_a_data_out, registers_1_b_data_out;
  wire [15:0] ADDRESS_BUS;

  Clock clock_1 (.out(clock_1_out));
  and and_1 (CLK, clock_1_out, ~in_1);  // AND_Gate
  LED led_1 (.in(in_1));
  LED led_2 (.in(in_3));
  LED led_3 (.in(in_5));
  LED led_4 (.in(in_7));
  LED led_5 (.in(in_9));
  LED led_6 (.in(in_11));
  LED led_7 (.in(in_13));
  LED led_8 (.in(in_15));
  LED led_9 (.in(in_17));
  LED led_10 (.in(in_19));
  LED led_11 (.in(in_21));
  LED led_12 (.in(in_23));
  LED led_13 (.in(in_25));
  LED led_14 (.in(in_27));
  LED led_15 (.in(in_29));
  LED led_16 (.in(in_31));
  Button u_RESET (.out(RESET));
  Registers registers_1 (
    .CLK(CLK), .RESET(RESET), .A_DATA_IN(DATA_BUS), .AI(in_11), .B_DATA_IN(DATA_BUS), .BI(in_15),
    .F_DATA_IN({F_SIGN, F_ZERO, FLAGS[1], F_CARRY}), .FI(in_31), .A_DATA_OUT(registers_1_a_data_out),
    .B_DATA_OUT(registers_1_b_data_out), .F_DATA_OUT(registers_1_f_data_out));
  ProgramCounter programcounter_1 (
    .CLK(CLK), .RESET(RESET), .J(in_9), .CO(in_7), .CE(in_5), .PC_ADDRESS_IN(ADDRESS_BUS),
    .PC_DATA_OUT(ADDRESS_BUS));
  LED led_17 (.in(in_2));
  LED led_18 (.in(in_4));
  LED led_19 (.in(in_6));
  LED led_20 (.in(in_8));
  LED led_21 (.in(in_10));
  LED led_22 (.in(in_12));
  LED led_23 (.in(in_14));
  LED led_24 (.in(in_16));
  LED led_25 (.in(in_18));
  LED led_26 (.in(in_20));
  LED led_27 (.in(in_22));
  LED led_28 (.in(in_24));
  LED led_29 (.in(in_26));
  LED led_30 (.in(in_28));
  LED led_31 (.in(in_30));
  LED led_32 (.in(in_32));
  assign DATA_BUS = in_13 ? registers_1_a_data_out : 8'bz;  // Controlled_Buffer controlled_buffer_1
  assign DATA_BUS = in_17 ? registers_1_b_data_out : 8'bz;  // Controlled_Buffer controlled_buffer_2
  // LedBar #(.inputtype("row")) ledbar_1: pin names not known; wires that end beside it: DATA_BUS
  // LedBar #(.inputtype("row"), .matrixcols(16)) ledbar_2: pin names not known; wires that end beside it: registers_1_f_data_out, ADDRESS_BUS
  ALU alu_1 (
    .A_DATA_IN(registers_1_a_data_out), .B_DATA_IN(registers_1_b_data_out), .OP_NOT(in_25), .OP_NAND(in_27),
    .CARRY_IN(F_CARRY), .OP_ADD(in_21), .OP_SUB(in_23), .OP_SR(in_29), .SIGN(F_SIGN), .ZERO(F_ZERO),
    .DATA_OUT(DATA_BUS), .CARRY_OUT(F_CARRY));
  Memory memory_1 (.CLK(CLK), .DATA_IN(DATA_BUS), .ADDR_IN(ADDRESS_BUS), .MI(in_4), .MO(in_6), .DATA_OUT(DATA_BUS));
  Pull_Resistor pull_resistor_1 (.node(FLAGS[1]));

  // Other names for the same wires on the sheet: AI = in_11; AO = in_13; BI = in_15; BO = in_17; DVE = in_18;
  //   DVW = in_20; FI = in_31; FLAGS (some bits) = {F_SIGN, F_ZERO, F_CARRY}; FO = in_2; HI = in_10; HLT = in_1;
  //   HO = in_12; IEND = in_3; INI = in_8; LI = in_14; LO = in_16; MI = in_4; MO = in_6; OPADD = in_21;
  //   OPNAND = in_27; OPNOT = in_25; OPSR = in_29; OPSUB = in_23; PCE = in_5; PCJ = in_9; PCO = in_7; RSO = in_19

  // Notes on the sheet:
  //   Tower
  //   Control signals
endmodule

module ProgramCounter (
  input  CLK,
  input  RESET,
  input  J,
  input  CO,
  input  CE,
  input  [15:0] PC_ADDRESS_IN,
  output [15:0] PC_DATA_OUT
);

  wire counter_1_carry;
  wire [15:0] counter_1_q;

  Counter #(.max('hffff), .width(16)) counter_1 (
    .clr(RESET), .load(J), .up(1'b1), .count(CE), .clk(CLK), .D(PC_ADDRESS_IN), .carry(counter_1_carry),
    .Q(counter_1_q));
  Pull_Resistor pull_resistor_1 (.node(counter_1_carry));
  assign PC_DATA_OUT = CO ? counter_1_q : 16'bz;  // Controlled_Buffer controlled_buffer_1

  // Notes on the sheet:
  //   Program Counter
endmodule

module ALU (
  input  [7:0] A_DATA_IN,
  input  [7:0] B_DATA_IN,
  input  OP_NOT,
  input  OP_NAND,
  input  CARRY_IN,
  input  OP_ADD,
  input  OP_SUB,
  input  OP_SR,
  output SIGN,
  output ZERO,
  output [7:0] DATA_OUT,
  output CARRY_OUT
);

  wire adder_1_cout, and_1_out, and_2_out, or_1_out, or_2_out;
  wire [7:0] adder_1_out, multiplexer_1_out, nand_1_out, not_1_out, not_2_out;

  or or_1 (or_1_out, CARRY_IN, OP_SUB);
  assign not_1_out = ~B_DATA_IN;  // NOT_Gate not_1, 8 bits wide
  or or_2 (or_2_out, OP_ADD, OP_SUB);
  assign not_2_out = ~A_DATA_IN;  // NOT_Gate not_2, 8 bits wide
  assign nand_1_out = ~(A_DATA_IN & B_DATA_IN);  // NAND_Gate nand_1, 8 bits wide
  Multiplexer #(.width(8)) multiplexer_1 (.in0(B_DATA_IN), .in1(not_1_out), .out(multiplexer_1_out), .sel(OP_SUB));
  assign DATA_OUT = OP_NOT ? not_2_out : 8'bz;  // Controlled_Buffer controlled_buffer_1
  assign DATA_OUT = OP_NAND ? nand_1_out : 8'bz;  // Controlled_Buffer controlled_buffer_2
  assign DATA_OUT = or_2_out ? adder_1_out : 8'bz;  // Controlled_Buffer controlled_buffer_3
  Adder adder_1 (.a(A_DATA_IN), .b(multiplexer_1_out), .out(adder_1_out), .cin(or_1_out), .cout(adder_1_cout));
  assign DATA_OUT = OP_SR ? {1'b0, A_DATA_IN[7:1]} : 8'bz;  // Controlled_Buffer controlled_buffer_4
  Pull_Resistor pull_resistor_1 (.node(DATA_OUT));
  and and_1 (and_1_out, or_2_out, adder_1_cout);
  and and_2 (and_2_out, A_DATA_IN[0], OP_SR);
  or or_3 (CARRY_OUT, and_1_out, and_2_out);
  nor nor_1 (ZERO, DATA_OUT[7], DATA_OUT[6], DATA_OUT[5], DATA_OUT[4], DATA_OUT[3], DATA_OUT[2], DATA_OUT[1], DATA_OUT[0]);

  assign SIGN = DATA_OUT[7];

  // Notes on the sheet:
  //   ALU
endmodule

module Memory (
  input  CLK,
  input  [7:0] DATA_IN,
  input  [15:0] ADDR_IN,
  input  MI,
  input  MO,
  output [7:0] DATA_OUT
);

  wire and_1_out, or_1_out;
  wire [7:0] multiplexer_1_out, ram_1_dout, rom_1_data;

  ROM #(.addrWidth(16)) rom_1 (.addr(ADDR_IN), .data(rom_1_data));
  or or_1 (or_1_out, ADDR_IN[14], ADDR_IN[15]);
  and and_1 (and_1_out, or_1_out, MI);
  RAM #(.addrWidth(16)) ram_1 (.addr(ADDR_IN), .we(and_1_out), .oe(MO), .clk(CLK), .din(DATA_IN), .dout(ram_1_dout));
  Multiplexer #(.width(8)) multiplexer_1 (.in0(rom_1_data), .in1(ram_1_dout), .out(multiplexer_1_out), .sel(or_1_out));
  assign DATA_OUT = MO ? multiplexer_1_out : 8'bz;  // Controlled_Buffer controlled_buffer_1

  // Notes on the sheet:
  //   contents of rom_1 (hex, n*v repeats v):
  //   f 8191*0 ff 53247*0 ff
  //   Memory
endmodule

module Registers (
  input  CLK,
  input  RESET,
  input  [7:0] A_DATA_IN,
  input  AI,
  input  [7:0] B_DATA_IN,
  input  BI,
  input  [3:0] F_DATA_IN,
  input  FI,
  output [7:0] A_DATA_OUT,
  output [7:0] B_DATA_OUT,
  output [3:0] F_DATA_OUT
);

  Register #(.trigger("falling")) A (.D(A_DATA_IN), .en(AI), .clk(CLK), .Q(A_DATA_OUT), .clr(RESET));
  Register #(.trigger("falling")) B (.D(B_DATA_IN), .en(BI), .clk(CLK), .Q(B_DATA_OUT), .clr(RESET));
  Register #(.trigger("falling"), .width(4)) F (.D(F_DATA_IN), .en(FI), .clk(CLK), .Q(F_DATA_OUT), .clr(RESET));

  // Notes on the sheet:
  //   Registers
endmodule
